// Logisim project circuito.circ as structural Verilog
module MUX (
  input  [3:0] A,
  input  [3:0] B,
  input  SELETOR,
  output [3:0] \SAÍDA 
);

  wire [3:0] and_1_out, and_2_out, not_1_out;

  assign and_1_out = A & not_1_out;  // AND_Gate and_1, 4 bits wide
  assign not_1_out = ~{4{SELETOR}};  // NOT_Gate not_1, 4 bits wide
  assign and_2_out = B & {4{SELETOR}};  // AND_Gate and_2, 4 bits wide
  assign \SAÍDA  = and_1_out | and_2_out;  // OR_Gate or_1, 4 bits wide
endmodule

module XOR (
  input  A,
  input  B,
  input  C,
  output \SAÍDA 
);

  wire and_1_out, and_2_out, and_3_out, and_4_out, or_1_out;

  and and_1 (and_1_out, ~A, B);  // AND_Gate
  and and_2 (and_2_out, A, ~B);  // AND_Gate
  or or_1 (or_1_out, and_1_out, and_2_out);
  and and_3 (and_3_out, ~or_1_out, C);  // AND_Gate
  and and_4 (and_4_out, or_1_out, ~C);  // AND_Gate
  or or_2 (\SAÍDA , and_3_out, and_4_out);
endmodule

// SUM
module SOMADOR (
  input  [3:0] A,
  input  [3:0] B,
  output [3:0] SUM,
  output CARRY
);

  wire and_1_out, and_2_out, and_3_out, and_4_out, and_5_out, and_6_out, and_7_out, and_8_out, and_9_out,
       and_10_out, and_11_out, and_12_out, or_1_out, or_2_out, or_3_out;

  and and_1 (and_1_out, A[0], B[0]);
  and and_2 (and_2_out, A[0], 1'b0);
  and and_3 (and_3_out, B[0], 1'b0);
  XOR xor_1 (.A(1'b0), .B(A[0]), .C(B[0]), .\SAÍDA (SUM[0]));
  or or_1 (or_1_out, and_1_out, and_2_out, and_3_out);
  XOR xor_2 (.A(or_1_out), .B(A[1]), .C(B[1]), .\SAÍDA (SUM[1]));
  and and_4 (and_4_out, A[1], B[1]);
  and and_5 (and_5_out, A[1], or_1_out);
  and and_6 (and_6_out, or_1_out, B[1]);
  or or_2 (or_2_out, and_4_out, and_5_out, and_6_out);
  XOR xor_3 (.A(or_2_out), .B(A[2]), .C(B[2]), .\SAÍDA (SUM[2]));
  and and_7 (and_7_out, A[2], B[2]);
  and and_8 (and_8_out, A[2], or_2_out);
  and and_9 (and_9_out, or_2_out, B[2]);
  or or_3 (or_3_out, and_7_out, and_8_out, and_9_out);
  XOR xor_4 (.A(or_3_out), .B(A[3]), .C(B[3]), .\SAÍDA (SUM[3]));
  and and_10 (and_10_out, A[3], B[3]);
  and and_11 (and_11_out, A[3], or_3_out);
  and and_12 (and_12_out, or_3_out, B[3]);
  or or_4 (CARRY, and_10_out, and_11_out, and_12_out);
endmodule

// FFD
module FLIP_FLOP_D (
  input  D,
  input  CLK,
  input  ENABLE,
  input  PRESET,
  input  CLEAR,
  output Q
);

  wire and_1_out, and_2_out, and_3_out, nor_2_out, not_1_out, not_2_out, not_3_out, not_4_out, or_1_out,
       or_2_out;

  not not_1 (not_1_out, CLK);
  not not_2 (not_2_out, not_1_out);
  not not_3 (not_3_out, not_2_out);
  and and_1 (and_1_out, not_3_out, CLK, ENABLE);
  not not_4 (not_4_out, D);
  and and_2 (and_2_out, not_4_out, and_1_out);
  and and_3 (and_3_out, and_1_out, D);
  or or_1 (or_1_out, CLEAR, and_2_out);
  or or_2 (or_2_out, and_3_out, PRESET);
  nor nor_1 (Q, or_1_out, nor_2_out);
  nor nor_2 (nor_2_out, Q, or_2_out);
endmodule

// REGIS
module REGISTRADOR (
  input  [3:0] D,
  input  CLK,
  input  ENABLE,
  input  CLEAR,
  input  ACTIVATE_PRESET,
  input  [3:0] PRESET,
  output [3:0] \SAÍDA 
);

  wire and_1_out, and_2_out, and_3_out, and_4_out, or_1_out, or_2_out, or_3_out, or_4_out;
  wire [3:0] \mux_1_saída ;

  FLIP_FLOP_D flip_flop_d_1 (
    .D(D[0]), .CLK(CLK), .ENABLE(ENABLE), .PRESET(\mux_1_saída [0]), .CLEAR(or_1_out), .Q(\SAÍDA [0]));
  or or_1 (or_1_out, and_1_out, CLEAR);
  and and_1 (and_1_out, ~\mux_1_saída [0], ACTIVATE_PRESET);  // AND_Gate
  FLIP_FLOP_D flip_flop_d_2 (
    .D(D[1]), .CLK(CLK), .ENABLE(ENABLE), .PRESET(\mux_1_saída [1]), .CLEAR(or_2_out), .Q(\SAÍDA [1]));
  or or_2 (or_2_out, and_2_out, CLEAR);
  and and_2 (and_2_out, ~\mux_1_saída [1], ACTIVATE_PRESET);  // AND_Gate
  MUX mux_1 (.A(4'b0000), .B(PRESET), .SELETOR(ACTIVATE_PRESET), .\SAÍDA (\mux_1_saída ));
  FLIP_FLOP_D flip_flop_d_3 (
    .D(D[2]), .CLK(CLK), .ENABLE(ENABLE), .PRESET(\mux_1_saída [2]), .CLEAR(or_3_out), .Q(\SAÍDA [2]));
  or or_3 (or_3_out, and_3_out, CLEAR);
  and and_3 (and_3_out, ~\mux_1_saída [2], ACTIVATE_PRESET);  // AND_Gate
  FLIP_FLOP_D flip_flop_d_4 (
    .D(D[3]), .CLK(CLK), .ENABLE(ENABLE), .PRESET(\mux_1_saída [3]), .CLEAR(or_4_out), .Q(\SAÍDA [3]));
  or or_4 (or_4_out, and_4_out, CLEAR);
  and and_4 (and_4_out, ~\mux_1_saída [3], ACTIVATE_PRESET);  // AND_Gate
endmodule

// =
module IGUAL (
  input  [3:0] A,
  input  [3:0] B,
  output \SAÍDA 
);

  wire xnor_1_out, xnor_2_out, xnor_3_out, xnor_4_out;

  xnor xnor_1 (xnor_1_out, B[0], A[0]);
  xnor xnor_2 (xnor_2_out, B[1], A[1]);
  xnor xnor_3 (xnor_3_out, B[2], A[2]);
  xnor xnor_4 (xnor_4_out, B[3], A[3]);
  and and_1 (\SAÍDA , xnor_1_out, xnor_2_out, xnor_3_out, xnor_4_out);
endmodule

// PRE
module PRESET (
  input  CLK,
  input  [3:0] MAXIMO,
  input  CLEAR,
  output [3:0] \SAÍDA 
);

  wire \igual_1_saída ;
  wire [3:0] \mux_1_saída , somador_1_sum;

  REGISTRADOR registrador_1 (
    .D(\mux_1_saída ), .CLK(CLK), .PRESET(4'b0000), .ENABLE(1'b1), .ACTIVATE_PRESET(1'b0), .CLEAR(CLEAR),
    .\SAÍDA (\SAÍDA ));
  SOMADOR somador_1 (.A(\SAÍDA ), .B(4'b0001), .SUM(somador_1_sum));  // open: CARRY
  IGUAL igual_1 (.\SAÍDA (\igual_1_saída ), .A(somador_1_sum), .B(MAXIMO));
  MUX mux_1 (.A(somador_1_sum), .B(4'b0000), .SELETOR(\igual_1_saída ), .\SAÍDA (\mux_1_saída ));
endmodule

// UNI
module UNIDADES (
  input  [3:0] E,
  output [3:0] E_plus,
  output S
);

  wire and_1_out, and_2_out, and_3_out, and_4_out, and_5_out, and_6_out, and_7_out, and_8_out, and_9_out,
       and_10_out, and_11_out, and_12_out, and_13_out, and_14_out, and_15_out, not_1_out, not_2_out,
       not_3_out, not_4_out, not_5_out, not_6_out, not_7_out, not_8_out, not_9_out, not_10_out, not_11_out,
       not_12_out, not_13_out, not_14_out, not_15_out, not_16_out, not_17_out;

  not not_1 (not_1_out, E[3]);
  not not_2 (not_2_out, E[2]);
  not not_3 (not_3_out, E[1]);
  not not_4 (not_4_out, E[0]);
  not not_5 (not_5_out, E[3]);
  not not_6 (not_6_out, E[3]);
  not not_7 (not_7_out, E[2]);
  not not_8 (not_8_out, E[1]);
  not not_9 (not_9_out, E[0]);
  not not_10 (not_10_out, E[3]);
  not not_11 (not_11_out, E[3]);
  not not_12 (not_12_out, E[1]);
  not not_13 (not_13_out, E[0]);
  not not_14 (not_14_out, E[2]);
  not not_15 (not_15_out, E[1]);
  not not_16 (not_16_out, E[0]);
  not not_17 (not_17_out, E[0]);
  and and_1 (and_1_out, E[3], E[1]);
  and and_2 (and_2_out, E[3], E[2]);
  and and_3 (and_3_out, not_1_out, not_2_out, not_3_out, not_4_out);
  and and_4 (and_4_out, E[3], E[0]);
  and and_5 (and_5_out, E[3], E[1]);
  and and_6 (and_6_out, E[3], E[2]);
  and and_7 (and_7_out, not_5_out, E[2], E[0]);
  and and_8 (and_8_out, not_6_out, E[2], E[1]);
  and and_9 (and_9_out, E[3], not_7_out, not_8_out, not_9_out);
  and and_10 (and_10_out, not_10_out, E[1], E[0]);
  and and_11 (and_11_out, not_11_out, E[2], not_12_out, not_13_out);
  and and_12 (and_12_out, E[3], not_14_out, not_15_out, not_16_out);
  or or_1 (E_plus[0], not_17_out, and_1_out, and_2_out);
  and and_13 (and_13_out, E[3], E[0]);
  and and_14 (and_14_out, E[3], E[1]);
  and and_15 (and_15_out, E[3], E[2]);
  or or_2 (E_plus[3], and_3_out, and_4_out, and_5_out, and_6_out);
  or or_3 (E_plus[2], and_7_out, and_8_out, and_9_out);
  or or_4 (E_plus[1], and_10_out, and_11_out, and_12_out);
  or or_5 (S, and_13_out, and_14_out, and_15_out);
endmodule

// DEZ
module DEZENAS (
  input  [3:0] E,
  output [3:0] E_plus,
  output S
);

  wire and_1_out, and_2_out, and_3_out, and_4_out, and_5_out, and_6_out, and_7_out, and_8_out, not_1_out,
       not_2_out, not_3_out, not_4_out, not_5_out, not_6_out, not_7_out, not_8_out, not_9_out;

  not not_1 (not_1_out, E[2]);
  not not_2 (not_2_out, E[1]);
  and and_1 (and_1_out, not_1_out, not_2_out, not_3_out);
  not not_3 (not_3_out, E[0]);
  and and_2 (and_2_out, E[2], E[0]);
  and and_3 (and_3_out, E[2], E[1]);
  not not_4 (not_4_out, E[3]);
  not not_5 (not_5_out, E[2]);
  not not_6 (not_6_out, E[3]);
  not not_7 (not_7_out, E[1]);
  not not_8 (not_8_out, E[0]);
  not not_9 (not_9_out, E[0]);
  and and_4 (and_4_out, E[2], E[1]);
  and and_5 (and_5_out, E[2], E[1]);
  and and_6 (and_6_out, E[2], E[0]);
  or or_1 (E_plus[2], and_1_out, and_2_out, and_3_out, E[3]);
  and and_7 (and_7_out, not_4_out, not_5_out, E[1], E[0]);
  or or_2 (E_plus[1], and_7_out, and_8_out);
  and and_8 (and_8_out, not_6_out, E[2], not_7_out, not_8_out);
  or or_3 (E_plus[0], not_9_out, and_4_out, E[3]);
  or or_4 (S, E[3], and_5_out, and_6_out);

  assign E_plus[3] = 1'b0;
endmodule

// CONTADOR
module CONTADOR_REGRESSIVO (
  input  CLK,
  input  [3:0] PRESET_US,
  input  [3:0] PRESET_DS,
  input  [3:0] PRESET_UM,
  input  [3:0] PRESET_DM,
  input  ENABLE,
  input  ACTIVATE_PRESET,
  input  CLEAR,
  output [3:0] US,
  output [3:0] DS,
  output [3:0] UM,
  output [3:0] DM,
  output ZEROU
);

  wire dezenas_1_s, \igual_1_saída , \igual_2_saída , \igual_3_saída , \igual_4_saída , unidades_1_s,
       unidades_2_s;
  wire [3:0] dezenas_1_e_plus, dezenas_2_e_plus, unidades_1_e_plus, unidades_2_e_plus;

  Hex_Digit_Display hex_digit_display_1 (.value(US));  // open: dp
  REGISTRADOR registrador_1 (
    .D(unidades_1_e_plus), .CLK(CLK), .PRESET(PRESET_US), .ENABLE(ENABLE), .ACTIVATE_PRESET(ACTIVATE_PRESET),
    .CLEAR(CLEAR), .\SAÍDA (US));
  UNIDADES unidades_1 (.E(US), .E_plus(unidades_1_e_plus), .S(unidades_1_s));
  REGISTRADOR registrador_2 (
    .D(dezenas_1_e_plus), .CLK(unidades_1_s), .PRESET(PRESET_DS), .ENABLE(ENABLE),
    .ACTIVATE_PRESET(ACTIVATE_PRESET), .CLEAR(CLEAR), .\SAÍDA (DS));
  Hex_Digit_Display hex_digit_display_2 (.value(DS));  // open: dp
  DEZENAS dezenas_1 (.E(DS), .E_plus(dezenas_1_e_plus), .S(dezenas_1_s));
  Hex_Digit_Display hex_digit_display_3 (.value(UM));  // open: dp
  REGISTRADOR registrador_3 (
    .D(unidades_2_e_plus), .CLK(dezenas_1_s), .PRESET(PRESET_UM), .ENABLE(ENABLE),
    .ACTIVATE_PRESET(ACTIVATE_PRESET), .CLEAR(CLEAR), .\SAÍDA (UM));
  UNIDADES unidades_2 (.E(UM), .E_plus(unidades_2_e_plus), .S(unidades_2_s));
  Hex_Digit_Display hex_digit_display_4 (.value(DM));  // open: dp
  REGISTRADOR registrador_4 (
    .D(dezenas_2_e_plus), .CLK(unidades_2_s), .PRESET(PRESET_DM), .ENABLE(ENABLE),
    .ACTIVATE_PRESET(ACTIVATE_PRESET), .CLEAR(CLEAR), .\SAÍDA (DM));
  DEZENAS dezenas_2 (.E(DM), .E_plus(dezenas_2_e_plus));  // open: S
  IGUAL igual_1 (.\SAÍDA (\igual_1_saída ), .A(DM), .B(4'b0000));
  IGUAL igual_2 (.\SAÍDA (\igual_2_saída ), .A(UM), .B(4'b0000));
  IGUAL igual_3 (.\SAÍDA (\igual_3_saída ), .A(DS), .B(4'b0000));
  IGUAL igual_4 (.\SAÍDA (\igual_4_saída ), .A(US), .B(4'b0000));
  and and_1 (ZEROU, \igual_1_saída , \igual_2_saída , \igual_3_saída , \igual_4_saída );
endmodule

// CRONO
module CRONOMETRO (
  input  CLK,
  input  CLK_DM,
  input  CLK_UM,
  input  CLK_DS,
  input  CLK_US,
  input  CLEAR_PRESET,
  input  ENABLE,
  input  ACTIVATE_PRESET,
  input  CLEAR,
  output [3:0] DM,
  output [3:0] UM,
  output [3:0] DS,
  output [3:0] US,
  output ZEROU
);

  wire and_1_out;
  wire [3:0] \preset_1_saída , \preset_2_saída , \preset_3_saída , \preset_4_saída ;

  Hex_Digit_Display hex_digit_display_1 (.value(\preset_1_saída ));  // open: dp
  PRESET preset_1 (.CLK(CLK_DM), .MAXIMO(4'b0110), .CLEAR(CLEAR_PRESET), .\SAÍDA (\preset_1_saída ));
  PRESET preset_2 (.CLK(CLK_UM), .MAXIMO(4'b1010), .CLEAR(CLEAR_PRESET), .\SAÍDA (\preset_2_saída ));
  PRESET preset_3 (.CLK(CLK_DS), .MAXIMO(4'b0110), .CLEAR(CLEAR_PRESET), .\SAÍDA (\preset_3_saída ));
  PRESET preset_4 (.CLK(CLK_US), .MAXIMO(4'b1010), .CLEAR(CLEAR_PRESET), .\SAÍDA (\preset_4_saída ));
  Hex_Digit_Display hex_digit_display_2 (.value(\preset_2_saída ));  // open: dp
  Hex_Digit_Display hex_digit_display_3 (.value(\preset_4_saída ));  // open: dp
  Hex_Digit_Display hex_digit_display_4 (.value(\preset_3_saída ));  // open: dp
  and and_1 (and_1_out, ENABLE, ~ZEROU);  // AND_Gate
  CONTADOR_REGRESSIVO contador_regressivo_1 (
    .CLK(CLK), .PRESET_US(\preset_4_saída ), .PRESET_DS(\preset_3_saída ), .PRESET_UM(\preset_2_saída ),
    .PRESET_DM(\preset_1_saída ), .ENABLE(and_1_out), .ACTIVATE_PRESET(ACTIVATE_PRESET), .CLEAR(CLEAR),
    .US(US), .DS(DS), .UM(UM), .DM(DM), .ZEROU(ZEROU));
endmodule

module Exemplo_Cronometro (
  input  ENABLE,
  input  SWITCH_PLAYER,
  input  ACTIVATE_PRESET
);

  wire and_1_out, CLEAR_out, CLEAR_PRESET_out, clock_1_out, cronometro_1_zerou, cronometro_2_zerou, DM_out,
       DS_out, multiplexer_1_out, multiplexer_2_out, not_1_out, UM_out, US_out;
  wire [3:0] cronometro_1_dm, cronometro_1_ds, cronometro_1_um, cronometro_1_us, cronometro_2_dm,
       cronometro_2_ds, cronometro_2_um, cronometro_2_us;

  Clock clock_1 (.out(clock_1_out));
  and and_1 (and_1_out, ENABLE, clock_1_out);
  Button CLEAR_PRESET (.out(CLEAR_PRESET_out));
  Button CLEAR (.out(CLEAR_out));
  Hex_Digit_Display hex_digit_display_1 (.value(cronometro_1_dm));  // open: dp
  Multiplexer #(.enable("false")) multiplexer_1 (
    .in0(SWITCH_PLAYER), .in1(1'b1), .out(multiplexer_1_out), .sel(cronometro_2_zerou));
  Hex_Digit_Display hex_digit_display_2 (.value(cronometro_1_ds));  // open: dp
  Hex_Digit_Display hex_digit_display_3 (.value(cronometro_1_um));  // open: dp
  CRONOMETRO cronometro_1 (
    .CLK(and_1_out), .CLK_DM(DM_out), .CLK_UM(UM_out), .CLK_DS(DS_out), .CLK_US(US_out),
    .DM(cronometro_1_dm), .UM(cronometro_1_um), .DS(cronometro_1_ds), .US(cronometro_1_us),
    .CLEAR_PRESET(CLEAR_PRESET_out), .ENABLE(multiplexer_1_out), .ACTIVATE_PRESET(ACTIVATE_PRESET),
    .CLEAR(CLEAR_out), .ZEROU(cronometro_1_zerou));
  Hex_Digit_Display hex_digit_display_4 (.value(cronometro_1_us));  // open: dp
  Button DM (.out(DM_out));
  Button UM (.out(UM_out));
  Button DS (.out(DS_out));
  Button US (.out(US_out));
  not not_1 (not_1_out, SWITCH_PLAYER);
  Hex_Digit_Display hex_digit_display_5 (.value(cronometro_2_dm));  // open: dp
  Multiplexer #(.enable("false")) multiplexer_2 (
    .in0(not_1_out), .in1(1'b1), .out(multiplexer_2_out), .sel(cronometro_1_zerou));
  Hex_Digit_Display hex_digit_display_6 (.value(cronometro_2_um));  // open: dp
  Hex_Digit_Display hex_digit_display_7 (.value(cronometro_2_us));  // open: dp
  Hex_Digit_Display hex_digit_display_8 (.value(cronometro_2_ds));  // open: dp
  CRONOMETRO cronometro_2 (
    .CLK(and_1_out), .CLK_DM(DM_out), .CLK_UM(UM_out), .CLK_DS(DS_out), .CLK_US(US_out),
    .DM(cronometro_2_dm), .UM(cronometro_2_um), .DS(cronometro_2_ds), .US(cronometro_2_us),
    .CLEAR_PRESET(CLEAR_PRESET_out), .ENABLE(multiplexer_2_out), .ACTIVATE_PRESET(ACTIVATE_PRESET),
    .CLEAR(CLEAR_out), .ZEROU(cronometro_2_zerou));
endmodule

module CORE (
  input  [3:0] A,
  input  [3:0] B,
  input  JOGADOR_ATUAL
);

  MUX mux_1 (.A(A), .B(B), .SELETOR(JOGADOR_ATUAL));  // open: SAÍDA
endmodule
